# Fritzing sketch Arduino Class LED with Switch (saved by Fritzing 0.8.7b)
breadboards: 1

parts:
  Arduino_Leonardo = Arduino Leonardo (Rev3b)
  LED1 = LED - 5mm [color="Red (633nm)" package="5 mm [THT]"]
  R1 = Resistor [tolerance=±5% resistance=330 package=THT]
  S1 = Pushbutton [package="[THT]"]

nets:
  N1: Arduino_Leonardo.D7, S1.Pin_3, S1.Pin_4
  5V: Arduino_Leonardo.5V
  N2: Arduino_Leonardo.GND, R1.Pin_1, S1.Pin_1, S1.Pin_2
  N3: Arduino_Leonardo.D8/A8, LED1.anode
  N4: LED1.cathode, R1.Pin_0
