# Fritzing sketch Arduino Class Piezo Speaker (saved by Fritzing 0.8.7b)
breadboards: 1

parts:
  Arduino_Leonardo = Arduino Leonardo (Rev3b)
  J1 = Piezo Speaker
  R1 = Resistor [tolerance=±5% resistance=1k package=THT]

nets:
  5V: Arduino_Leonardo.5V
  N1: Arduino_Leonardo.GND, J1.pin1
  N2: Arduino_Leonardo.D12/A11, R1.Pin_1
  N3: J1.pin2, R1.Pin_0
