# Fritzing sketch Arduino Class Single LED (saved by Fritzing 0.8.7b)
breadboards: 1

parts:
  Arduino_Leonardo = Arduino Leonardo (Rev3b)
  LED1 = LED - 5mm [color="Red (633nm)" package="5 mm [THT]"]
  R1 = Resistor [tolerance=±5% resistance=220 package=THT]

nets:
  N1: Arduino_Leonardo.D7, LED1.anode
  5V: Arduino_Leonardo.5V
  N2: Arduino_Leonardo.GND, R1.Pin_1
  N3: LED1.cathode, R1.Pin_0
