# Fritzing sketch Arduino Class Three Segment Simon (saved by Fritzing 0.8.7b)
breadboards: 1

parts:
  J1 = Piezo Speaker
  S1 = Pushbutton [package="[THT]"]
  S2 = Pushbutton [package="[THT]"]
  S3 = Pushbutton [package="[THT]"]
  Arduino_Leonardo = Arduino Leonardo (Rev3b)
  LED1 = LED - 5mm [color="Red (633nm)" package="5 mm [THT]"]
  LED2 = LED - 5mm [color="Green (555nm)" package="5 mm [THT]"]
  LED3 = LED - 5mm [color="Yellow (595nm)" package="5 mm [THT]"]
  R1 = Resistor [tolerance=±5% resistance=220 package=THT]
  R3 = Resistor [tolerance=±5% resistance=220 package=THT]
  R4 = Resistor [tolerance=±5% resistance=220 package=THT]
  R5 = Resistor [tolerance=±5% resistance=220 package=THT]

nets:
  N1: J1.pin1, R5.Pin_0
  N2: J1.pin2, Arduino_Leonardo.D12/A11
  N3: S1.Pin_1, S1.Pin_2, Arduino_Leonardo.D2/SDA
  N4: S1.Pin_3, S1.Pin_4, S2.Pin_3, S2.Pin_4, S3.Pin_3, S3.Pin_4, Arduino_Leonardo.GND, LED1.cathode, LED2.cathode, LED3.cathode, R5.Pin_1
  N5: S2.Pin_1, S2.Pin_2, Arduino_Leonardo.D3_PWM/SCL, Arduino_Leonardo.SCL
  N6: S3.Pin_1, S3.Pin_2, Arduino_Leonardo.D4/A6
  5V: Arduino_Leonardo.5V
  N7: Arduino_Leonardo.D8/A8, R4.Pin_1
  N8: Arduino_Leonardo.D9_PWM/A9, R3.Pin_1
  N9: Arduino_Leonardo.D10_PWM/A10, R1.Pin_1
  N10: LED1.anode, R4.Pin_0
  N11: LED2.anode, R3.Pin_0
  N12: LED3.anode, R1.Pin_0
