# Fritzing sketch Arduino Class Two LEDs (saved by Fritzing 0.8.7b)
breadboards: 1

parts:
  Arduino_Leonardo = Arduino Leonardo (Rev3b)
  LED1 = LED - 5mm [color="Red (633nm)" package="5 mm [THT]"]
  R1 = Resistor [tolerance=±5% resistance=330 package=THT]
  R2 = Resistor [tolerance=±20% resistance=330 package=THT]
  LED2 = LED - 5mm [color="Green (555nm)" package="5 mm [THT]"]

nets:
  N1: Arduino_Leonardo.D7, LED1.anode
  5V: Arduino_Leonardo.5V
  N2: Arduino_Leonardo.GND, R1.Pin_1, R2.Pin_1
  N3: Arduino_Leonardo.D8/A8, LED2.anode
  N4: LED1.cathode, R1.Pin_0
  N5: R2.Pin_0, LED2.cathode
