# Fritzing sketch Three Segment Simon Layout (saved by Fritzing 0.7.10b)
breadboards: 1

parts:
  Arduino1 = Arduino
  LED1 = LED - 5mm [color="Red (633nm)" package="5 mm [THT]"]  # not connected
  J1 = Piezo Speaker

nets:
  N1: Arduino1.GND, J1.pin1
